// Logisim project nand2tetris.circ as structural Verilog
module Not (
  input  Input,
  output Output
);

  nand nand_1 (Output, Input, Input);
endmodule

module And (
  input  in_1,
  input  in_2,
  output out_3
);

  wire nand_1_out;

  nand nand_1 (nand_1_out, in_1, in_2);
  Not not_1 (.Input(nand_1_out), .Output(out_3));
endmodule

module Or (
  input  a,
  input  b,
  output out_3
);

  wire not_1_output, not_2_output;

  Not not_1 (.Input(a), .Output(not_1_output));
  Not not_2 (.Input(b), .Output(not_2_output));
  nand nand_1 (out_3, not_1_output, not_2_output);
endmodule

module Xor (
  input  a,
  input  b,
  output out_3
);

  wire nand_1_out, nand_2_out, not_1_output, not_2_output;

  Not not_1 (.Input(a), .Output(not_1_output));
  Not not_2 (.Input(b), .Output(not_2_output));
  nand nand_1 (nand_1_out, not_1_output, b);
  nand nand_2 (nand_2_out, a, not_2_output);
  nand nand_3 (out_3, nand_1_out, nand_2_out);
endmodule
